// Logisim project aiAlu.circ as structural Verilog: 13 circuits, main circuit and8bit
module and8bit (
  input  E,
  input  [7:0] A,
  input  [7:0] B,
  output [7:0] out_4
);

  wire [7:0] and_1_out, bit_extender_1_out;

  assign bit_extender_1_out = {{7{E}}, E};  // Bit_Extender bit_extender_1
  assign and_1_out = A & B;  // AND_Gate and_1, 8 bits wide
  assign out_4 = bit_extender_1_out & and_1_out;  // AND_Gate and_2, 8 bits wide

  // Notes on the sheet:
  //   AND a 8 bit
endmodule

module or8bit (
  input  ENABLE,
  input  [7:0] A,
  input  [7:0] B,
  output [7:0] out_4
);

  wire [7:0] bit_extender_1_out, or_1_out;

  assign bit_extender_1_out = {{7{ENABLE}}, ENABLE};  // Bit_Extender bit_extender_1
  assign or_1_out = A | B;  // OR_Gate or_1, 8 bits wide
  assign out_4 = bit_extender_1_out & or_1_out;  // AND_Gate and_1, 8 bits wide

  // Notes on the sheet:
  //   OR a 8 BIT
endmodule

module xor8bit (
  input  E,
  input  [7:0] A,
  input  [7:0] B,
  output [7:0] out_4
);

  wire [7:0] bit_extender_1_out, not_1_out, or_1_out;

  assign bit_extender_1_out = {{7{E}}, E};  // Bit_Extender bit_extender_1
  assign or_1_out = A | B;  // OR_Gate or_1, 8 bits wide
  assign not_1_out = ~or_1_out;  // NOT_Gate not_1, 8 bits wide
  assign out_4 = bit_extender_1_out & not_1_out;  // AND_Gate and_1, 8 bits wide

  // Notes on the sheet:
  //   XOR a 8 BIT
endmodule

module halfAdder (
  input  a,
  input  b,
  output S,
  output C
);

  and and_1 (C, a, b);
  xor xor_1 (S, a, b);
endmodule

module Full_Adder (
  input  C0,
  input  a,
  input  b,
  output S,
  output C1
);

  wire and_1_out, and_2_out, and_3_out, xor_1_out;

  xor xor_1 (xor_1_out, a, b);
  and and_1 (and_1_out, C0, a);
  and and_2 (and_2_out, a, b);
  and and_3 (and_3_out, C0, b);
  xor xor_2 (S, xor_1_out, C0);
  or or_1 (C1, and_1_out, and_2_out, and_3_out);
endmodule

module CPL2 (
  input  [7:0] in_1,
  output C,
  output [7:0] out_3
);

  wire halfadder_1_c, halfadder_2_c, halfadder_3_c, halfadder_4_c, halfadder_5_c, halfadder_6_c,
       halfadder_7_c;
  wire [7:0] not_1_out;

  assign not_1_out = ~in_1;  // NOT_Gate not_1, 8 bits wide
  halfAdder halfadder_1 (.a(1'b1), .b(not_1_out[0]), .S(out_3[0]), .C(halfadder_1_c));
  halfAdder halfadder_2 (.a(not_1_out[2]), .b(halfadder_3_c), .S(out_3[2]), .C(halfadder_2_c));
  halfAdder halfadder_3 (.a(not_1_out[1]), .b(halfadder_1_c), .S(out_3[1]), .C(halfadder_3_c));
  halfAdder halfadder_4 (.a(not_1_out[4]), .b(halfadder_5_c), .S(out_3[4]), .C(halfadder_4_c));
  halfAdder halfadder_5 (.a(not_1_out[3]), .b(halfadder_2_c), .S(out_3[3]), .C(halfadder_5_c));
  halfAdder halfadder_6 (.a(not_1_out[6]), .b(halfadder_7_c), .S(out_3[6]), .C(halfadder_6_c));
  halfAdder halfadder_7 (.a(not_1_out[5]), .b(halfadder_4_c), .S(out_3[5]), .C(halfadder_7_c));
  halfAdder halfadder_8 (.a(not_1_out[7]), .b(halfadder_6_c), .S(out_3[7]), .C(C));
endmodule

module Adder_4_bits (
  input  c0,
  input  a0,
  input  b0,
  input  a1,
  input  b1,
  input  a2,
  input  b2,
  input  a3,
  input  b3,
  output s0,
  output s1,
  output s2,
  output s3,
  output C
);

  wire full_adder_1_c1, full_adder_2_c1, full_adder_3_c1;

  Full_Adder full_adder_1 (.S(s0), .C1(full_adder_1_c1), .C0(c0), .a(a0), .b(b0));
  Full_Adder full_adder_2 (.S(s1), .C1(full_adder_2_c1), .C0(full_adder_1_c1), .a(a1), .b(b1));
  Full_Adder full_adder_3 (.S(s2), .C1(full_adder_3_c1), .C0(full_adder_2_c1), .a(a2), .b(b2));
  Full_Adder full_adder_4 (.S(s3), .C1(C), .C0(full_adder_3_c1), .a(a3), .b(b3));
endmodule

module Overflow__8_bits_adder (
  input  a7,
  input  b7,
  input  a6,
  input  b6,
  input  a5,
  input  b5,
  input  a4,
  input  b4,
  input  a3,
  input  b3,
  input  a2,
  input  b2,
  input  a1,
  input  b1,
  input  a0,
  input  b0,
  input  in_17,
  output overflow,
  output s7,
  output s6,
  output s5,
  output s4,
  output s3,
  output s2,
  output s1,
  output s0
);

  wire adder_4_bits_2_c;

  Adder_4_bits adder_4_bits_1 (
    .s0(s4), .s1(s5), .s2(s6), .s3(s7), .a0(a4), .a1(a5), .a2(a6), .a3(a7), .b0(b4), .b1(b5), .b2(b6),
    .b3(b7), .c0(adder_4_bits_2_c), .C(overflow));
  Adder_4_bits adder_4_bits_2 (
    .s0(s0), .s1(s1), .s2(s2), .s3(s3), .a0(a0), .a1(a1), .a2(a2), .a3(a3), .b0(b0), .b1(b1), .b2(b2),
    .b3(b3), .c0(in_17), .C(adder_4_bits_2_c));
endmodule

module NOT_A (
  input  in_1,
  input  [7:0] in_2,
  output [7:0] out_3
);

  wire [7:0] bit_extender_1_out, not_1_out;

  assign not_1_out = ~in_2;  // NOT_Gate not_1, 8 bits wide
  assign bit_extender_1_out = {{7{in_1}}, in_1};  // Bit_Extender bit_extender_1
  assign out_3 = bit_extender_1_out & not_1_out;  // AND_Gate and_1, 8 bits wide

  // Notes on the sheet:
  //   NOT a 8 BIT
endmodule

module MUX_da_2_a_1 (
  input  in_1,
  input  in_2,
  input  in_3,
  output out_4
);

  wire and_1_out, and_2_out, not_1_out;

  not not_1 (not_1_out, in_1);
  and and_1 (and_1_out, not_1_out, in_2);
  and and_2 (and_2_out, in_1, in_3);
  or or_1 (out_4, and_1_out, and_2_out);
endmodule

module NOT_B (
  input  in_1,
  input  [7:0] B,
  output [7:0] out_3
);

  wire [7:0] bit_extender_1_out, not_1_out;

  assign not_1_out = ~B;  // NOT_Gate not_1, 8 bits wide
  assign bit_extender_1_out = {{7{in_1}}, in_1};  // Bit_Extender bit_extender_1
  assign out_3 = bit_extender_1_out & not_1_out;  // AND_Gate and_1, 8 bits wide

  // Notes on the sheet:
  //   NOT a 8 BIT
endmodule

module Mux_da_4_a_1 (
  input  in_1,
  input  in_2,
  input  in_3,
  input  in_4,
  input  in_5,
  input  in_6,
  output out_7
);

  wire and_1_out, and_2_out, and_3_out, and_4_out, not_1_out, not_2_out;

  not not_1 (not_1_out, in_1);
  not not_2 (not_2_out, in_2);
  and and_1 (and_1_out, not_1_out, not_2_out, in_3);
  and and_2 (and_2_out, not_1_out, in_2, in_4);
  and and_3 (and_3_out, in_1, not_2_out, in_5);
  and and_4 (and_4_out, in_1, in_2, in_6);
  or or_1 (out_7, and_1_out, and_2_out, and_3_out, and_4_out);
endmodule

module AiLogic (
  input  in_1,
  input  in_2,
  input  in_3,
  input  in_4,
  input  in_5,
  input  in_6,
  input  [7:0] a,
  input  [7:0] b,
  output [7:0] out_9
);

  wire and_1_out;
  wire [7:0] and8bit_1_out_4, bit_extender_1_out, not_a_1_out_3, not_b_1_out_3, or8bit_1_out_4,
       xor8bit_1_out_4;

  and and_1 (and_1_out, 1'b0, in_1);
  assign bit_extender_1_out = {{7{and_1_out}}, and_1_out};  // Bit_Extender bit_extender_1
  NOT_A not_a_1 (.in_1(in_3), .in_2(a), .out_3(not_a_1_out_3));
  NOT_B not_b_1 (.in_1(in_2), .B(b), .out_3(not_b_1_out_3));
  xor8bit xor8bit_1 (.E(in_4), .A(a), .B(b), .out_4(xor8bit_1_out_4));
  or8bit or8bit_1 (.ENABLE(in_5), .A(a), .B(b), .out_4(or8bit_1_out_4));
  assign out_9 = bit_extender_1_out | not_b_1_out_3 | not_a_1_out_3 | xor8bit_1_out_4 | or8bit_1_out_4 | and8bit_1_out_4;  // OR_Gate or_1, 8 bits wide
  and8bit and8bit_1 (.E(in_6), .A(a), .B(b), .out_4(and8bit_1_out_4));
endmodule
